# Fritzing sketch Ograda jedna tipka (shema) (saved by Fritzing 0.9.3b)
breadboards: 1

parts:
  Part1 = Arduino Uno (Rev3)
  S1 = Pushbutton [package="[THT]"]
  S2 = Pushbutton [package="[SMD]"]
  S3 = Momentary Switch [package=ksa_sealed_tac_switch]
  R1 = Resistor [tolerance=±5% resistance=220 package=THT]
  R2 = Resistor [tolerance=±5% resistance=220 package=THT]
  R3 = Resistor [tolerance=±5% resistance=220 package=THT]
  S4 = H-Bridge with L298N
  Power_plug1 = Power plug
  M1 = DC Motor
  LED1 = LED - 3mm [color="Red (633nm)" package="3 mm [THT]"]

nets:
  N1: Part1.A0, LED1.anode
  N2: Part1.D8, S2.Pin_1, S2.Pin_2, R2.Pin_1
  N3: Part1.D9_PWM, S4.IN2
  N4: Part1.D10_PWM/SS, S4.IN1
  N5: Part1.D11_PWM/MOSI, S4.ENA
  N6: Part1.D12/MISO, S3.1, R1.Pin_1
  N7: Part1.D13/SCK, S1.Pin_1, S1.Pin_2, R3.Pin_1
  5V: Part1.5V, S1.Pin_3, S1.Pin_4, S2.Pin_3, S2.Pin_4, S3.4, S4.5V
  N8: Part1.GND, LED1.cathode
  GND: R1.Pin_0, R2.Pin_0, R3.Pin_0, S4.GND, Power_plug1.GND
  12V: S4.12V, Power_plug1.VCC
  N9: S4.M1-01, M1.pin_2
  N10: S4.M1-02, M1.pin_1

notes:
  Tipka za otvaranje <--> D8
  Limit switch (otvorena vrata) <--> D12
  Limit switch (zatvorena vrata) <--> D13
  H BRIDGE
  IN 1 <--> D10
  IN 2 <--> D9
  ENA <--> D11
  +12V <--> +12V (Napajanje)
  GND <--> GND (Napajanje)
  LED <--> A0 i GND
  OUT1 <--> Motor 1
  OUT2 <--> Motor 2
  Za postavljanje lampe (umjesto LED-ice) veće od 5V potrebno je ugraditi relej
  RELEJ
  5V <--> 5V
  GND <--> GND
  S <--> A0

custom parts:
  H-Bridge with L298N: h-bridge
