# Fritzing sketch RFID ograda final (shema) (saved by Fritzing 0.9.3b)
breadboards: 1

parts:
  S1 = Pushbutton [package="[THT]"]
  S2 = Pushbutton [package="[THT]"]
  M1 = DC Motor
  Power_plug1 = Power plug
  R1 = Resistor [tolerance=±5% resistance=220 package=THT]
  R2 = Resistor [tolerance=±5% resistance=220 package=THT]
  Part1 = Arduino Uno (Rev3)
  S3 = H-Bridge with L298N
  LED1 = LED - 5mm [color="Red (633nm)" package="5 mm [THT]"]
  Part2 = RFID USB Reader

nets:
  N1: S1.Pin_1, S1.Pin_2, R1.Pin_1, Part1.D7
  5V: S1.Pin_3, S1.Pin_4, S2.Pin_3, S2.Pin_4, Part1.5V, S3.5V
  N2: S2.Pin_1, S2.Pin_2, R2.Pin_1, Part1.D6_PWM
  N3: M1.pin_1, S3.M1-02
  N4: M1.pin_2, S3.M1-01
  VCC: Power_plug1.VCC, S3.12V
  GND: Power_plug1.GND, R1.Pin_0, R2.Pin_0, S3.GND
  N5: Part1.A0, LED1.anode
  N6: Part1.D9_PWM, S3.IN2
  N7: Part1.D10_PWM/SS, S3.IN1
  N8: Part1.D11_PWM/MOSI, S3.ENA
  GND_2: Part1.GND, LED1.cathode, Part2.GND
  N9: Part1.D1/TX, Part2.TX-O
  N10: Part1.D2, Part2.TX-O-RS232
  N11: Part1.D3_PWM, Part2.ANT1
  N12: Part1.D4, Part2.ANT2
  N13: Part1.D5_PWM, Part2.CP
  3V3: Part1.3V3, Part2.VCC

notes:
  Limit switch (otvorena vrata)<--> D6
  Limit switch (zatvorena vrata) <--> D7
  H BRIDGE
  IN1 <--> D10
  IN2 <-->D9
  ENA <-->D11
  12V <--> 12V (Napajanje)
  GND <--> GND (Napajanje)
  OUT 1 <--> Motor 1
  OUT 2 <--> Motor 2
  RFID
  RST <--> D5
  SDA <--> D4
  MOSI <--> D3
  MISO <--> D2
  SCK <--> D1
  3.3V <--> 3.3V (Arduino)
  GND <--> GND (Arduino)
  LED
  A0 i GND (Arduino)
  Za ugrađivanje lampe (umjesto LED-ice) veće od 5V potrebno je ugraditi relej
  RELEJ
  5V <--> 5V
  GND <--> GND
  S <--> A0

custom parts:
  H-Bridge with L298N: h-bridge
